# Fritzing sketch sketch_1 (saved by Fritzing 0.9.4)
breadboards: 1

parts:
  LED1 = LED - 5mm [color="Red (633nm)" package="5 mm [THT]"]
  R1 = Resistor [tolerance=±5% resistance=220 package=THT]
  S1 = Pushbutton [package="[THT]"]
  VCC1 = 4 x AAA Battery Mount
  S2 = Pushbutton [package="[THT]"]
  R2 = Resistor [tolerance=±5% resistance=220 package=THT]
  LED2 = LED - 5mm [color="Orange (620nm)" package="5 mm [THT]"]
  LED3 = LED - 5mm [color="Green (555nm)" package="5 mm [THT]"]
  R3 = Resistor [tolerance=±5% resistance=220 package=THT]
  S3 = Pushbutton [package="[THT]"]

nets:
  N1: LED1.cathode, R1.Pin_1
  N2: LED1.anode, VCC1.+, LED2.anode, LED3.anode
  N3: R1.Pin_0, S1.Pin_1, S1.Pin_2
  N4: S1.Pin_3, S1.Pin_4, VCC1.-, S2.Pin_3, S2.Pin_4, S3.Pin_3, S3.Pin_4
  N5: S2.Pin_1, S2.Pin_2, R2.Pin_0
  N6: R2.Pin_1, LED2.cathode
  N7: LED3.cathode, R3.Pin_1
  N8: R3.Pin_0, S3.Pin_1, S3.Pin_2
